// Logisim project dmux.circ as structural Verilog: 1 circuit, main circuit main
module main (
  input  In,
  input  Sel,
  output A,
  output B
);

  wire xor_1_out;

  xor xor_1 (xor_1_out, In, Sel);
  and and_1 (A, In, xor_1_out);
  and and_2 (B, In, Sel);
endmodule
